// Digital circuit COMPUTER.dig as structural Verilog
module COMPUTER (
  input  CLK,
  input  [15:0] INSTR
);

  wire ctrl_unit_1_p5, ctrl_unit_1_p7, ctrl_unit_1_p10;
  wire [1:0] ctrl_unit_1_p9, ctrl_unit_1_p11;
  wire [2:0] ctrl_unit_1_p2, ctrl_unit_1_p3, ctrl_unit_1_p4, ctrl_unit_1_p6;
  wire [7:0] _8_register_bank_1_rd1, _8_register_bank_1_rd2, _256b_mem_1_rd, alu_8_1_s, ctrl_unit_1_p8,
       multiplexer_1_out, multiplexer_2_out, multiplexer_3_out, PC_plus_1_s, PC_q;

  Multiplexer #(.Bits(8), .Selector_Bits(2)) multiplexer_1 (
    .sel(ctrl_unit_1_p11), .in_0(PC_plus_1_s), .in_1(ctrl_unit_1_p8), .in_2(_8_register_bank_1_rd1),
    .in_3({8{1'b0}}), .out(multiplexer_1_out));
  REGISTER_8 PC (.D(multiplexer_1_out), .E(1'b1), .CLK(CLK), .Q(PC_q));
  // CTRL_UNIT ctrl_unit_1: pin names not known; wires that end beside it: INSTR, ctrl_unit_1_p2, ctrl_unit_1_p3, ctrl_unit_1_p4, ctrl_unit_1_p5, ctrl_unit_1_p6, ctrl_unit_1_p7, ctrl_unit_1_p8, ctrl_unit_1_p9, ctrl_unit_1_p10, ctrl_unit_1_p11
  ADD_8 PC_plus_1 (.Cin(1'b0), .A(PC_q), .B(8'h1), .S(PC_plus_1_s));  // open: Cout
  _8_REGISTER_BANK _8_register_bank_1 (
    .A1(ctrl_unit_1_p2), .A2(ctrl_unit_1_p3), .A3(ctrl_unit_1_p4), .WD3(multiplexer_3_out),
    .WE3(ctrl_unit_1_p5), .CLK(CLK), .RD1(_8_register_bank_1_rd1), .RD2(_8_register_bank_1_rd2));
  Multiplexer #(.Bits(8)) multiplexer_2 (
    .sel(ctrl_unit_1_p7), .in_0(_8_register_bank_1_rd2), .in_1(ctrl_unit_1_p8), .out(multiplexer_2_out));
  ALU_8 alu_8_1 (.A(_8_register_bank_1_rd1), .B(multiplexer_2_out), .OP(ctrl_unit_1_p6), .S(alu_8_1_s));
  _256B_MEM _256b_mem_1 (
    .A(alu_8_1_s), .WD(_8_register_bank_1_rd2), .WE(ctrl_unit_1_p10), .CLK(CLK), .RD(_256b_mem_1_rd));
  Multiplexer #(.Selector_Bits(2), .Bits(8)) multiplexer_3 (
    .sel(ctrl_unit_1_p9), .in_0(alu_8_1_s), .in_1(_256b_mem_1_rd), .in_2(PC_plus_1_s), .in_3({8{1'b0}}),
    .out(multiplexer_3_out));
endmodule
